# Fritzing sketch schematic (saved by Fritzing 0.9.3b)

parts:
  Raspberry_Pi_1 = Raspberry Pi 4 [part_number=RPI-4-b]
  U1 = LIPO-2000mAh [package=lipo-2000]
  AUX_SPEAKER = SPEAKER [package=pcb_mount_speaker]  # not connected
  USB_MICROPHONE = USB connector [package=THT]  # not connected
  128x32_OLED_I2C_DISPLAY = Grove OLED 128x96

nets:
  N1: Raspberry_Pi_1.GPIO2, 128x32_OLED_I2C_DISPLAY.SDA
  N2: Raspberry_Pi_1.GPIO3, 128x32_OLED_I2C_DISPLAY.SCL
  GND: Raspberry_Pi_1.GND, U1.-, 128x32_OLED_I2C_DISPLAY.GND
  5V: Raspberry_Pi_1.5V, U1.+, 128x32_OLED_I2C_DISPLAY.VCC

custom parts:
  Raspberry Pi 4: The RPi4, a faster version of the awesome Raspberry Pi 2 B ARM Board with 40 pin gpio. Ready for special Raspberry Pi B+ and RPi2 Hat (Hardware attached (on) top)
